// Logisim project Four_Bits_Add_Sub.circ as structural Verilog: 2 circuits, main circuit Add_Sub_4Bits
module Add_Sub_4Bits (
  input  [3:0] A,
  input  [3:0] B,
  input  Add_Sub,
  output [3:0] R,
  output Zero,
  output Overflow
);

  // Probe on A
  // Probe on B
  // Probe on R

  // Notes on the sheet:
  //   YOUR NAME AND STUDENT NUMBER HERE
  //   MAKE SURE THAT YOU OPEN THIS PROJECT IN "LOGISIM-EVOLUTION"
endmodule

module Add_1Bit (
  input  Cin,
  input  A,
  input  B,
  output Sum,
  output Cout
);


  // Notes on the sheet:
  //   YOUR NAME AND STUDENT NUMBER HERE
  //   MAKE SURE THAT YOU OPENED THIS PROJECT IN "LOGISIM-EVOLUTION"
endmodule
