// Logisim project RAM_16_Nibbles_Read_Write.circ as structural Verilog: 2 circuits, main circuit RAM_16_Nibbles
// Clk
module RAM_16_Nibbles (
  input  [3:0] Data,
  input  Read_Write,
  input  [3:0] Address,
  output [3:0] RAM_OUT
);

  wire Clk_out;

  // Probe on Data
  Clock Clk (.out(Clk_out));
  // Probe on Address
  Nibble nibble_1 ();  // open: Data, Read_Write, Enable, Clk, Nibble_Out
  // Probe on RAM_OUT

  // Notes on the sheet:
  //   When Read_Write = 0 performs read, otherwise performs write
  //   MAKE SURE THAT YOU OPEN THIS PROJECT IN "LOGISIM-EVOLUTION"
endmodule

module Nibble (
  input  [3:0] Data,
  input  Read_Write,
  input  Enable,
  input  Clk,
  output [3:0] Nibble_Out
);

  // Probe on Data
  // Probe on Nibble_Out

  // Notes on the sheet:
  //   When Read_Write = 0 performs read, otherwise performs write
  //   MAKE SURE THAT YOU OPEN THIS PROJECT IN "LOGISIM-EVOLUTION"
endmodule
